# Fritzing sketch ejercicio02 (saved by Fritzing 0.9.4)

parts:
  U1 = NodeMCU V3.0
  HC-SR04_Sensor_1 = HC-SR04 Ultrasonic Distance Sensor

nets:
  N1: U1.D1, HC-SR04_Sensor_1.TRIG
  N2: U1.D2, HC-SR04_Sensor_1.ECHO
  3V3: U1.3V3, HC-SR04_Sensor_1.VCC
  GND: U1.GND, HC-SR04_Sensor_1.GND

custom parts:
  NodeMCU V3.0: ESP8266 based NodeMCU
